// Digital circuit 2bitmultiplier.dig as structural Verilog
module _2bitmultiplier (
  input  A,
  input  B,
  input  C,
  input  D,
  output P0,
  output P1,
  output P2,
  output P3
);

  wire and_3_out, and_4_out, and_5_out, and_6_out, or_1_out;

  and and_1 (P3, A, B, C, D);
  or or_1 (or_1_out, ~B, ~D);  // Or
  and and_2 (P2, A, C, or_1_out);
  and and_3 (and_3_out, ~A, B, C);  // And
  and and_4 (and_4_out, B, C, ~D);  // And
  and and_5 (and_5_out, A, ~C, D);  // And
  and and_6 (and_6_out, A, ~C, D);  // And
  and and_7 (P0, B, D);
  or or_2 (P1, and_3_out, and_4_out, and_5_out, and_6_out);
endmodule
