// Digital circuit 4bitadder.dig as structural Verilog
module _4bitadder (
  input  A0,
  input  B0,
  input  A1,
  input  B1,
  input  A2,
  input  B2,
  input  A3,
  input  B3,
  input  C_in,
  output S0,
  output S1,
  output S2,
  output S3,
  output overflow
);

  wire _1bitfulladder_1_c_out, _1bitfulladder_2_c_out, _1bitfulladder_3_c_out;

  _1bitfulladder _1bitfulladder_1 (.A(A0), .B(B0), .C_in(C_in), .Sum(S0), .C_out(_1bitfulladder_1_c_out));
  _1bitfulladder _1bitfulladder_2 (
    .A(A1), .B(B1), .C_in(_1bitfulladder_1_c_out), .Sum(S1), .C_out(_1bitfulladder_2_c_out));
  _1bitfulladder _1bitfulladder_3 (
    .A(A2), .B(B2), .C_in(_1bitfulladder_2_c_out), .Sum(S2), .C_out(_1bitfulladder_3_c_out));
  _1bitfulladder _1bitfulladder_4 (.A(A3), .B(B3), .C_in(_1bitfulladder_3_c_out), .Sum(S3), .C_out(overflow));
endmodule
